# Fritzing sketch Schema (saved by Fritzing 0.9.3b)
breadboards: 2

parts:
  Part1 = Arduino Uno (Rev3)
  Part2 = KY-006 Passive Buzzer Module [package="Breakout board"]
  LED7 = smd LED [color="Yellow (595nm)" package="1206 [SMD]"]
  LED8 = smd LED [color="Red (635nm)" package="1206 [SMD]"]
  R7 = Resistor [tolerance=±5% resistance=220 package="0603 [SMD]"]
  R8 = Resistor [tolerance=±5% resistance=220 package="0603 [SMD]"]

nets:
  N1: Part1.D8, Part2.S
  N2: Part1.D12/MISO, R8.Pin_0
  N3: Part1.D13/SCK, R7.Pin_0
  N4: Part1.GND, Part2.-, LED7.cathode, LED8.cathode
  N5: LED7.anode, R7.Pin_1
  N6: LED8.anode, R8.Pin_1

custom parts:
  KY-006 Passive Buzzer Module: Passive Piezoelectric Buzzer Module Keyes KY-006, it can produce a range of sound tones depending on the input frequency.
